// Logisim project 2023.11.13.MUX.circ as structural Verilog: 2 circuits, main circuit 8 to 1 MUX
module _8_to_1_MUX (
  input  in_1,
  input  in_2,
  input  in_3,
  input  in_4,
  input  in_5,
  input  in_6,
  input  in_7,
  input  in_8,
  input  in_9,
  input  in_10,
  input  in_11,
  output out_12
);

  wire and_1_out, and_2_out, and_3_out, and_4_out, and_5_out, and_6_out, and_7_out, and_8_out, not_1_out,
       not_2_out, not_3_out, not_4_out, not_5_out, not_6_out, not_7_out, not_8_out, not_9_out, not_10_out,
       not_11_out, not_12_out;

  not not_1 (not_1_out, in_1);
  not not_2 (not_2_out, in_2);
  not not_3 (not_3_out, in_2);
  not not_4 (not_4_out, in_1);
  not not_5 (not_5_out, in_3);
  not not_6 (not_6_out, in_3);
  not not_7 (not_7_out, in_1);
  not not_8 (not_8_out, in_3);
  not not_9 (not_9_out, in_2);
  not not_10 (not_10_out, in_3);
  not not_11 (not_11_out, in_2);
  not not_12 (not_12_out, in_1);
  and and_1 (and_1_out, in_3, in_2, in_4, in_1);
  and and_2 (and_2_out, in_3, in_2, in_5, not_1_out);
  and and_3 (and_3_out, in_3, not_2_out, in_6, in_1);
  and and_4 (and_4_out, in_3, not_3_out, in_7, not_4_out);
  and and_5 (and_5_out, not_5_out, in_2, in_8, in_1);
  and and_6 (and_6_out, not_6_out, in_2, in_9, not_7_out);
  and and_7 (and_7_out, not_8_out, not_9_out, in_10, in_1);
  and and_8 (and_8_out, not_10_out, not_11_out, in_11, not_12_out);
  or or_1 (out_12, and_1_out, and_2_out, and_3_out, and_4_out, and_5_out, and_6_out, and_7_out, and_8_out);
endmodule

module _2_to_1_MUX (
  input  in_1,
  input  in_2,
  input  in_3,
  output out_4
);

  wire and_1_out, and_2_out, not_1_out;

  not not_1 (not_1_out, in_1);
  and and_1 (and_1_out, in_2, not_1_out);
  and and_2 (and_2_out, in_3, in_1);
  or or_1 (out_4, and_1_out, and_2_out);
endmodule
