// Logisim project 2023.11.19.Storage Element.circ as structural Verilog: 15 circuits, main circuit Basic SR latch
module Basic_SR_latch (
  input  R,
  input  S,
  output Q,
  output Q_prime
);

  nor nor_1 (Q, R, Q_prime);
  nor nor_2 (Q_prime, Q, S);
endmodule

module Gated_SR_latch (
  input  R,
  input  Clk,
  input  S,
  output Q,
  output Q_prime
);

  wire and_1_out, and_2_out;

  and and_1 (and_1_out, R, Clk);
  and and_2 (and_2_out, Clk, S);
  Basic_SR_latch basic_sr_latch_1 (.R(and_1_out), .Q(Q), .Q_prime(Q_prime), .S(and_2_out));
endmodule

module Gated_D_latch (
  input  D,
  input  Clk,
  output Q,
  output Q_prime
);

  wire and_1_out, and_2_out, not_1_out;

  not not_1 (not_1_out, D);
  and and_1 (and_1_out, not_1_out, Clk);
  and and_2 (and_2_out, Clk, D);
  nor nor_1 (Q, and_1_out, Q_prime);
  nor nor_2 (Q_prime, Q, and_2_out);
endmodule

module Positive_Edge_Triggered_D_flip_flop (
  input  D,
  input  Clock,
  output Q,
  output Q_prime
);

  wire gated_d_latch_1_q, not_1_out;

  not not_1 (not_1_out, Clock);
  Gated_D_latch gated_d_latch_1 (.D(D), .Clk(not_1_out), .Q(gated_d_latch_1_q));  // open: Q_prime
  Gated_D_latch gated_d_latch_2 (.D(gated_d_latch_1_q), .Clk(Clock), .Q(Q), .Q_prime(Q_prime));
endmodule

module Negative_Edge_Triggered_D_flip_flop (
  input  D,
  input  Clock,
  output Q,
  output Q_prime
);

  wire gated_d_latch_1_q, not_1_out;

  Gated_D_latch gated_d_latch_1 (.D(D), .Clk(Clock), .Q(gated_d_latch_1_q));  // open: Q_prime
  not not_1 (not_1_out, Clock);
  Gated_D_latch gated_d_latch_2 (.D(gated_d_latch_1_q), .Clk(not_1_out), .Q(Q), .Q_prime(Q_prime));
endmodule

module Negative_Edge_Triggered_D_flip_flop__Preset_Clear (
  input  Preset_n,
  input  D,
  input  Clock,
  input  Clear_n,
  output Q,
  output Q_prime
);

  wire nand_1_out, nand_2_out, nand_3_out, nand_4_out, nand_5_out, nand_6_out, not_1_out, not_2_out;

  not not_1 (not_1_out, D);
  nand nand_1 (nand_1_out, D, Clock);
  nand nand_2 (nand_2_out, Clock, not_1_out);
  nand nand_3 (nand_3_out, Preset_n, nand_1_out, nand_4_out);
  nand nand_4 (nand_4_out, nand_3_out, nand_2_out, Clear_n);
  not not_2 (not_2_out, Clock);
  nand nand_5 (nand_5_out, nand_3_out, not_2_out);
  nand nand_6 (nand_6_out, not_2_out, nand_4_out);
  nand nand_7 (Q, Preset_n, nand_5_out, Q_prime);
  nand nand_8 (Q_prime, Q, nand_6_out, Clear_n);
endmodule

module D_flip_flop (
  input  in_1,
  input  in_2,
  output out_3,
  output out_4
);

  wire nand_1_out, nand_2_out, nand_3_out, nand_4_out;

  nand nand_1 (nand_1_out, nand_4_out, nand_2_out);
  nand nand_2 (nand_2_out, nand_1_out, in_1);
  nand nand_3 (nand_3_out, nand_2_out, in_1, nand_4_out);
  nand nand_4 (nand_4_out, nand_3_out, in_2);
  nand nand_5 (out_3, nand_2_out, out_4);
  nand nand_6 (out_4, out_3, nand_3_out);
endmodule

module JK_flip_flop (
  input  Preset_n,
  input  J,
  input  K,
  input  Clock,
  input  Clear_n,
  output Q,
  output Q_prime
);

  wire and_1_out, and_2_out, not_1_out, not_2_out, or_1_out;

  not not_1 (not_1_out, K);
  and and_1 (and_1_out, Q_prime, J);
  and and_2 (and_2_out, not_1_out, Q);
  or or_1 (or_1_out, and_1_out, and_2_out);
  not not_2 (not_2_out, Clock);
  Negative_Edge_Triggered_D_flip_flop__Preset_Clear negative_edge_triggered_d_flip_flop_preset_clear_1 (
    .Preset_n(Preset_n), .D(or_1_out), .Clock(not_2_out), .Clear_n(Clear_n), .Q(Q), .Q_prime(Q_prime));
endmodule

module T_flip_flop__Preset_Clear (
  input  Preset_n,
  input  T,
  input  Clock,
  input  Clear_n,
  output Q,
  output Q_prime
);

  wire not_1_out, xor_1_out;

  not not_1 (not_1_out, Clock);
  xor xor_1 (xor_1_out, Q, T);
  Negative_Edge_Triggered_D_flip_flop__Preset_Clear negative_edge_triggered_d_flip_flop_preset_clear_1 (
    .Preset_n(Preset_n), .D(xor_1_out), .Clock(not_1_out), .Clear_n(Clear_n), .Q(Q), .Q_prime(Q_prime));
endmodule

module Shift_Register (
  input  Shift_0_Load_1,
  input  Serial_input,
  input  Clock,
  input  Clear_n,
  input  in_5,
  input  in_6,
  input  in_7,
  input  in_8,
  output Q3,
  output Q2,
  output Q1,
  output Q0
);

  wire n2_to_1_mux_1_out_4, n2_to_1_mux_2_out_4, n2_to_1_mux_3_out_4, n2_to_1_mux_4_out_4, not_1_out;

  not not_1 (not_1_out, Clock);
  _2_to_1_MUX u_2_to_1_mux_1 (.in_2(Serial_input), .in_3(in_5), .out_4(n2_to_1_mux_1_out_4), .in_1(Shift_0_Load_1));
  Negative_Edge_Triggered_D_flip_flop__Preset_Clear negative_edge_triggered_d_flip_flop_preset_clear_1 (
    .Preset_n(1'b1), .D(n2_to_1_mux_1_out_4), .Clock(not_1_out), .Clear_n(Clear_n), .Q(Q3));  // open: Q_prime
  _2_to_1_MUX u_2_to_1_mux_2 (.in_2(Q3), .in_3(in_6), .out_4(n2_to_1_mux_2_out_4), .in_1(Shift_0_Load_1));
  Negative_Edge_Triggered_D_flip_flop__Preset_Clear negative_edge_triggered_d_flip_flop_preset_clear_2 (
    .Preset_n(1'b1), .D(n2_to_1_mux_2_out_4), .Clock(not_1_out), .Clear_n(Clear_n), .Q(Q2));  // open: Q_prime
  _2_to_1_MUX u_2_to_1_mux_3 (.in_2(Q2), .in_3(in_7), .out_4(n2_to_1_mux_3_out_4), .in_1(Shift_0_Load_1));
  Negative_Edge_Triggered_D_flip_flop__Preset_Clear negative_edge_triggered_d_flip_flop_preset_clear_3 (
    .Preset_n(1'b1), .D(n2_to_1_mux_3_out_4), .Clock(not_1_out), .Clear_n(Clear_n), .Q(Q1));  // open: Q_prime
  _2_to_1_MUX u_2_to_1_mux_4 (.in_2(Q1), .in_3(in_8), .out_4(n2_to_1_mux_4_out_4), .in_1(Shift_0_Load_1));
  Negative_Edge_Triggered_D_flip_flop__Preset_Clear negative_edge_triggered_d_flip_flop_preset_clear_4 (
    .Preset_n(1'b1), .D(n2_to_1_mux_4_out_4), .Clock(not_1_out), .Clear_n(Clear_n), .Q(Q0));  // open: Q_prime
endmodule

module _3bit_Counter__T_flip_flop (
  input  Preset_n,
  input  T,
  input  Clock,
  input  Clear_n,
  output out_5,
  output out_6,
  output out_7,
  output out_8
);

  wire and_1_out, and_2_out;

  T_flip_flop__Preset_Clear t_flip_flop_preset_clear_1 (
    .T(T), .Clock(Clock), .Q(out_6), .Clear_n(Clear_n), .Preset_n(Preset_n));  // open: Q_prime
  and and_1 (and_1_out, T, out_6);
  T_flip_flop__Preset_Clear t_flip_flop_preset_clear_2 (
    .T(and_1_out), .Clock(Clock), .Q(out_7), .Clear_n(Clear_n), .Preset_n(Preset_n));  // open: Q_prime
  and and_2 (and_2_out, and_1_out, out_7);
  T_flip_flop__Preset_Clear t_flip_flop_preset_clear_3 (
    .T(and_2_out), .Clock(Clock), .Q(out_8), .Clear_n(Clear_n), .Preset_n(Preset_n));  // open: Q_prime
  and and_3 (out_5, and_2_out, out_8);
endmodule

module _4bit_Counter__D_flip_flop (
  input  D0,
  input  D1,
  input  D2,
  input  D3,
  input  Count_0_Load_1,
  input  En,
  input  Clock,
  input  Clear_n,
  output Q0,
  output Q1,
  output Q2,
  output Q3
);

  wire and_1_out, and_2_out, and_3_out, n2_to_1_mux_1_out_4, n2_to_1_mux_2_out_4, n2_to_1_mux_3_out_4,
       n2_to_1_mux_4_out_4, not_1_out, xor_1_out, xor_2_out, xor_3_out, xor_4_out;

  _2_to_1_MUX u_2_to_1_mux_1 (.in_2(xor_1_out), .in_3(D0), .out_4(n2_to_1_mux_1_out_4), .in_1(Count_0_Load_1));
  not not_1 (not_1_out, Clock);
  Negative_Edge_Triggered_D_flip_flop__Preset_Clear negative_edge_triggered_d_flip_flop_preset_clear_1 (
    .Preset_n(1'b1), .D(n2_to_1_mux_1_out_4), .Clock(not_1_out), .Clear_n(Clear_n), .Q(Q0));  // open: Q_prime
  xor xor_1 (xor_1_out, En, Q0);
  _2_to_1_MUX u_2_to_1_mux_2 (.in_2(xor_2_out), .in_3(D1), .out_4(n2_to_1_mux_2_out_4), .in_1(Count_0_Load_1));
  xor xor_2 (xor_2_out, and_1_out, Q1);
  and and_1 (and_1_out, En, Q0);
  Negative_Edge_Triggered_D_flip_flop__Preset_Clear negative_edge_triggered_d_flip_flop_preset_clear_2 (
    .Preset_n(1'b1), .D(n2_to_1_mux_2_out_4), .Clock(not_1_out), .Clear_n(Clear_n), .Q(Q1));  // open: Q_prime
  _2_to_1_MUX u_2_to_1_mux_3 (.in_2(xor_3_out), .in_3(D2), .out_4(n2_to_1_mux_3_out_4), .in_1(Count_0_Load_1));
  and and_2 (and_2_out, and_1_out, Q1);
  Negative_Edge_Triggered_D_flip_flop__Preset_Clear negative_edge_triggered_d_flip_flop_preset_clear_3 (
    .Preset_n(1'b1), .D(n2_to_1_mux_3_out_4), .Clock(not_1_out), .Clear_n(Clear_n), .Q(Q2));  // open: Q_prime
  xor xor_3 (xor_3_out, and_2_out, Q2);
  _2_to_1_MUX u_2_to_1_mux_4 (.in_2(xor_4_out), .in_3(D3), .out_4(n2_to_1_mux_4_out_4), .in_1(Count_0_Load_1));
  xor xor_4 (xor_4_out, and_3_out, Q3);
  and and_3 (and_3_out, and_2_out, Q2);
  Negative_Edge_Triggered_D_flip_flop__Preset_Clear negative_edge_triggered_d_flip_flop_preset_clear_4 (
    .Preset_n(1'b1), .D(n2_to_1_mux_4_out_4), .Clock(not_1_out), .Clear_n(Clear_n), .Q(Q3));  // open: Q_prime
endmodule

module Modulo_6_Counter (
  input  En,
  input  Clock,
  input  Clear_n,
  output Q0,
  output Q1,
  output Q2
);

  wire and_1_out, and_2_out, and_3_out, n2_to_1_mux_1_out_4, n2_to_1_mux_2_out_4, n2_to_1_mux_3_out_4,
       not_1_out, xor_1_out, xor_2_out, xor_3_out;

  _2_to_1_MUX u_2_to_1_mux_1 (.in_2(xor_1_out), .in_3(1'b0), .out_4(n2_to_1_mux_1_out_4), .in_1(and_3_out));
  not not_1 (not_1_out, Clock);
  xor xor_1 (xor_1_out, En, Q0);
  Negative_Edge_Triggered_D_flip_flop__Preset_Clear negative_edge_triggered_d_flip_flop_preset_clear_1 (
    .Preset_n(1'b1), .D(n2_to_1_mux_1_out_4), .Clock(not_1_out), .Clear_n(Clear_n), .Q(Q0));  // open: Q_prime
  _2_to_1_MUX u_2_to_1_mux_2 (.in_2(xor_2_out), .in_3(1'b0), .out_4(n2_to_1_mux_2_out_4), .in_1(and_3_out));
  xor xor_2 (xor_2_out, and_1_out, Q1);
  and and_1 (and_1_out, En, Q0);
  Negative_Edge_Triggered_D_flip_flop__Preset_Clear negative_edge_triggered_d_flip_flop_preset_clear_2 (
    .Preset_n(1'b1), .D(n2_to_1_mux_2_out_4), .Clock(not_1_out), .Clear_n(Clear_n), .Q(Q1));  // open: Q_prime
  _2_to_1_MUX u_2_to_1_mux_3 (.in_2(xor_3_out), .in_3(1'b0), .out_4(n2_to_1_mux_3_out_4), .in_1(and_3_out));
  and and_2 (and_2_out, and_1_out, Q1);
  and and_3 (and_3_out, Q0, Q2);
  xor xor_3 (xor_3_out, and_2_out, Q2);
  Negative_Edge_Triggered_D_flip_flop__Preset_Clear negative_edge_triggered_d_flip_flop_preset_clear_3 (
    .Preset_n(1'b1), .D(n2_to_1_mux_3_out_4), .Clock(not_1_out), .Clear_n(Clear_n), .Q(Q2));  // open: Q_prime
endmodule

module ring_Counter (
  input  Start,
  input  Clock,
  input  Clear_n,
  output Q3,
  output Q2,
  output Q1,
  output Q0
);

  wire not_1_out;

  not not_1 (not_1_out, Clock);
  Negative_Edge_Triggered_D_flip_flop__Preset_Clear negative_edge_triggered_d_flip_flop_preset_clear_1 (
    .Preset_n(Start), .D(Q0), .Clock(not_1_out), .Clear_n(Clear_n), .Q(Q3));  // open: Q_prime
  Negative_Edge_Triggered_D_flip_flop__Preset_Clear negative_edge_triggered_d_flip_flop_preset_clear_2 (
    .Preset_n(1'b1), .D(Q3), .Clock(not_1_out), .Clear_n(Clear_n), .Q(Q2));  // open: Q_prime
  Negative_Edge_Triggered_D_flip_flop__Preset_Clear negative_edge_triggered_d_flip_flop_preset_clear_3 (
    .Preset_n(1'b1), .D(Q2), .Clock(not_1_out), .Clear_n(Clear_n), .Q(Q1));  // open: Q_prime
  Negative_Edge_Triggered_D_flip_flop__Preset_Clear negative_edge_triggered_d_flip_flop_preset_clear_4 (
    .Preset_n(1'b1), .D(Q1), .Clock(not_1_out), .Clear_n(Clear_n), .Q(Q0));  // open: Q_prime
endmodule

module Johnson_Counter (
  input  Clock,
  input  Clear_n,
  output Q3,
  output Q2,
  output Q1,
  output Q0
);

  wire negative_edge_triggered_d_flip_flop_preset_clear_4_q_prime, not_1_out;

  not not_1 (not_1_out, Clock);
  Negative_Edge_Triggered_D_flip_flop__Preset_Clear negative_edge_triggered_d_flip_flop_preset_clear_1 (
    .Preset_n(1'b1), .D(negative_edge_triggered_d_flip_flop_preset_clear_4_q_prime), .Clock(not_1_out),
    .Clear_n(Clear_n), .Q(Q3));  // open: Q_prime
  Negative_Edge_Triggered_D_flip_flop__Preset_Clear negative_edge_triggered_d_flip_flop_preset_clear_2 (
    .Preset_n(1'b1), .D(Q3), .Clock(not_1_out), .Clear_n(Clear_n), .Q(Q2));  // open: Q_prime
  Negative_Edge_Triggered_D_flip_flop__Preset_Clear negative_edge_triggered_d_flip_flop_preset_clear_3 (
    .Preset_n(1'b1), .D(Q2), .Clock(not_1_out), .Clear_n(Clear_n), .Q(Q1));  // open: Q_prime
  Negative_Edge_Triggered_D_flip_flop__Preset_Clear negative_edge_triggered_d_flip_flop_preset_clear_4 (
    .Preset_n(1'b1), .D(Q1), .Clock(not_1_out), .Clear_n(Clear_n), .Q(Q0),
    .Q_prime(negative_edge_triggered_d_flip_flop_preset_clear_4_q_prime));
endmodule
