// Logisim project 2024.07.03.연산장치.circ as structural Verilog: 4 circuits, main circuit Ripple_Carry_Adder
module Ripple_Carry_Adder (
  input  in_1,
  input  in_2,
  input  in_3,
  input  in_4,
  input  in_5,
  input  in_6,
  input  in_7,
  input  in_8,
  input  in_9,
  input  in_10,
  input  in_11,
  input  in_12,
  input  in_13,
  input  in_14,
  input  in_15,
  input  in_16,
  input  in_17,
  output out_18,
  output out_19,
  output out_20,
  output out_21,
  output out_22,
  output out_23,
  output out_24,
  output out_25,
  output out_26
);

  wire fulladder_1_carry_out, fulladder_2_carry_out, fulladder_3_carry_out, fulladder_4_carry_out,
       fulladder_5_carry_out, fulladder_6_carry_out, fulladder_7_carry_out, fulladder_8_carry_out,
       xor2_1_out0, xor2_2_out0, xor2_3_out0, xor2_4_out0, xor2_5_out0, xor2_6_out0, xor2_7_out0, xor2_8_out0;

  XOR2 xor2_1 (.IN0(in_3), .IN1(in_1), .OUT0(xor2_1_out0));
  XOR2 xor2_2 (.IN0(in_5), .IN1(in_1), .OUT0(xor2_2_out0));
  XOR2 xor2_3 (.IN0(in_7), .IN1(in_1), .OUT0(xor2_3_out0));
  XOR2 xor2_4 (.IN0(in_9), .IN1(in_1), .OUT0(xor2_4_out0));
  XOR2 xor2_5 (.IN0(in_11), .IN1(in_1), .OUT0(xor2_5_out0));
  XOR2 xor2_6 (.IN0(in_13), .IN1(in_1), .OUT0(xor2_6_out0));
  XOR2 xor2_7 (.IN0(in_15), .IN1(in_1), .OUT0(xor2_7_out0));
  XOR2 xor2_8 (.IN0(in_17), .IN1(in_1), .OUT0(xor2_8_out0));
  FullAdder fulladder_1 (
    .IN0(in_2), .IN1(xor2_1_out0), .Carry_in(in_1), .Sum(out_18), .Carry_out(fulladder_1_carry_out));
  FullAdder fulladder_2 (
    .IN0(in_4), .IN1(xor2_2_out0), .Carry_in(fulladder_1_carry_out), .Sum(out_19),
    .Carry_out(fulladder_2_carry_out));
  FullAdder fulladder_3 (
    .IN0(in_6), .IN1(xor2_3_out0), .Carry_in(fulladder_2_carry_out), .Sum(out_20),
    .Carry_out(fulladder_3_carry_out));
  FullAdder fulladder_4 (
    .IN0(in_8), .IN1(xor2_4_out0), .Carry_in(fulladder_3_carry_out), .Sum(out_21),
    .Carry_out(fulladder_4_carry_out));
  FullAdder fulladder_5 (
    .IN0(in_10), .IN1(xor2_5_out0), .Carry_in(fulladder_4_carry_out), .Sum(out_22),
    .Carry_out(fulladder_5_carry_out));
  FullAdder fulladder_6 (
    .IN0(in_12), .IN1(xor2_6_out0), .Carry_in(fulladder_5_carry_out), .Sum(out_23),
    .Carry_out(fulladder_6_carry_out));
  FullAdder fulladder_7 (
    .IN0(in_14), .IN1(xor2_7_out0), .Carry_in(fulladder_6_carry_out), .Sum(out_24),
    .Carry_out(fulladder_7_carry_out));
  FullAdder fulladder_8 (
    .IN0(in_16), .IN1(xor2_8_out0), .Carry_in(fulladder_7_carry_out), .Sum(out_25),
    .Carry_out(fulladder_8_carry_out));
  XOR2 xor2_9 (.IN0(fulladder_8_carry_out), .IN1(fulladder_7_carry_out), .OUT0(out_26));
endmodule

module Mult_2comp_4bit (
  input  in_1,
  input  in_2,
  input  in_3,
  input  in_4,
  input  in_5,
  input  in_6,
  input  in_7,
  input  in_8,
  output out_9,
  output out_10,
  output out_11,
  output out_12,
  output out_13,
  output out_14,
  output out_15
);

  wire and2_2_out0, and2_3_out0, and2_4_out0, and2_5_out0, and2_6_out0, and2_7_out0, and2_8_out0,
       and2_9_out0, and2_10_out0, and2_11_out0, and2_12_out0, and2_13_out0, and2_14_out0, and2_15_out0,
       and2_16_out0, fulladder_1_carry_out, fulladder_2_carry_out, fulladder_2_sum, fulladder_3_carry_out,
       fulladder_3_sum, fulladder_4_sum, fulladder_5_carry_out, fulladder_6_carry_out, fulladder_6_sum,
       fulladder_7_carry_out, fulladder_7_sum, fulladder_8_sum, fulladder_9_carry_out,
       fulladder_10_carry_out, fulladder_11_carry_out;

  AND2 and2_1 (.IN0(in_5), .IN1(in_1), .OUT0(out_9));
  AND2 and2_2 (.IN0(in_6), .IN1(in_1), .OUT0(and2_2_out0));
  AND2 and2_3 (.IN0(in_7), .IN1(in_1), .OUT0(and2_3_out0));
  AND2 and2_4 (.IN0(in_8), .IN1(in_1), .OUT0(and2_4_out0));
  AND2 and2_5 (.IN0(in_2), .IN1(in_5), .OUT0(and2_5_out0));
  AND2 and2_6 (.IN0(in_2), .IN1(in_6), .OUT0(and2_6_out0));
  AND2 and2_7 (.IN0(in_2), .IN1(in_7), .OUT0(and2_7_out0));
  AND2 and2_8 (.IN0(in_2), .IN1(in_8), .OUT0(and2_8_out0));
  FullAdder fulladder_1 (
    .IN0(and2_2_out0), .IN1(and2_5_out0), .Carry_in(1'b0), .Sum(out_10), .Carry_out(fulladder_1_carry_out));
  FullAdder fulladder_2 (
    .IN0(and2_3_out0), .IN1(and2_6_out0), .Carry_in(fulladder_1_carry_out), .Sum(fulladder_2_sum),
    .Carry_out(fulladder_2_carry_out));
  FullAdder fulladder_3 (
    .IN0(and2_4_out0), .IN1(and2_7_out0), .Carry_in(fulladder_2_carry_out), .Sum(fulladder_3_sum),
    .Carry_out(fulladder_3_carry_out));
  FullAdder fulladder_4 (
    .IN0(1'b0), .IN1(and2_8_out0), .Carry_in(fulladder_3_carry_out), .Sum(fulladder_4_sum));  // open: Carry_out
  AND2 and2_9 (.IN0(in_3), .IN1(in_5), .OUT0(and2_9_out0));
  FullAdder fulladder_5 (
    .IN0(fulladder_2_sum), .IN1(and2_9_out0), .Carry_in(1'b0), .Sum(out_11), .Carry_out(fulladder_5_carry_out));
  AND2 and2_10 (.IN0(in_3), .IN1(in_6), .OUT0(and2_10_out0));
  FullAdder fulladder_6 (
    .IN0(fulladder_3_sum), .IN1(and2_10_out0), .Carry_in(fulladder_5_carry_out), .Sum(fulladder_6_sum),
    .Carry_out(fulladder_6_carry_out));
  AND2 and2_11 (.IN0(in_3), .IN1(in_7), .OUT0(and2_11_out0));
  FullAdder fulladder_7 (
    .IN0(fulladder_4_sum), .IN1(and2_11_out0), .Carry_in(fulladder_6_carry_out), .Sum(fulladder_7_sum),
    .Carry_out(fulladder_7_carry_out));
  AND2 and2_12 (.IN0(in_3), .IN1(in_8), .OUT0(and2_12_out0));
  FullAdder fulladder_8 (
    .IN0(1'b0), .IN1(and2_12_out0), .Carry_in(fulladder_7_carry_out), .Sum(fulladder_8_sum));  // open: Carry_out
  AND2 and2_13 (.IN0(in_4), .IN1(in_5), .OUT0(and2_13_out0));
  AND2 and2_14 (.IN0(in_4), .IN1(in_6), .OUT0(and2_14_out0));
  AND2 and2_15 (.IN0(in_4), .IN1(in_7), .OUT0(and2_15_out0));
  AND2 and2_16 (.IN0(in_4), .IN1(in_8), .OUT0(and2_16_out0));
  FullAdder fulladder_9 (
    .IN0(fulladder_6_sum), .IN1(and2_13_out0), .Carry_in(1'b0), .Sum(out_12),
    .Carry_out(fulladder_9_carry_out));
  FullAdder fulladder_10 (
    .IN0(fulladder_7_sum), .IN1(and2_14_out0), .Carry_in(fulladder_9_carry_out), .Sum(out_13),
    .Carry_out(fulladder_10_carry_out));
  FullAdder fulladder_11 (
    .IN0(fulladder_8_sum), .IN1(and2_15_out0), .Carry_in(fulladder_10_carry_out), .Sum(out_14),
    .Carry_out(fulladder_11_carry_out));
  FullAdder fulladder_12 (
    .IN0(1'b0), .IN1(and2_16_out0), .Carry_in(fulladder_11_carry_out), .Sum(out_15));  // open: Carry_out
endmodule

module Mult_4bit (
  input  in_1,
  input  in_2,
  input  in_3,
  input  in_4,
  input  in_5,
  input  in_6,
  input  in_7,
  input  in_8,
  output out_9,
  output out_10,
  output out_11,
  output out_12,
  output out_13,
  output out_14,
  output out_15,
  output out_16
);

  wire and2_2_out0, and2_3_out0, and2_4_out0, and2_5_out0, and2_6_out0, and2_7_out0, and2_8_out0,
       and2_9_out0, and2_10_out0, fulladder_1_carry_out, fulladder_2_carry_out, fulladder_2_sum,
       fulladder_3_carry_out, fulladder_3_sum, fulladder_4_carry_out, fulladder_4_sum, fulladder_5_carry_out,
       fulladder_6_carry_out, fulladder_6_sum, fulladder_7_carry_out, fulladder_7_sum, fulladder_8_carry_out,
       fulladder_8_sum, fulladder_9_carry_out, fulladder_10_carry_out, fulladder_11_carry_out,
       fulladder_12_carry_out, nand_1_out0, nand_2_out0, nand_3_out0, nand_4_out0, nand_5_out0, nand_6_out0;

  AND2 and2_1 (.IN0(in_5), .IN1(in_1), .OUT0(out_9));
  AND2 and2_2 (.IN0(in_6), .IN1(in_1), .OUT0(and2_2_out0));
  AND2 and2_3 (.IN0(in_7), .IN1(in_1), .OUT0(and2_3_out0));
  NAND nand_1 (.IN0(in_8), .OUT0(nand_1_out0), .IN1(in_1));
  AND2 and2_4 (.IN0(in_2), .IN1(in_5), .OUT0(and2_4_out0));
  AND2 and2_5 (.IN0(in_2), .IN1(in_6), .OUT0(and2_5_out0));
  AND2 and2_6 (.IN0(in_2), .IN1(in_7), .OUT0(and2_6_out0));
  NAND nand_2 (.IN0(in_2), .OUT0(nand_2_out0), .IN1(in_8));
  FullAdder fulladder_1 (
    .IN0(and2_2_out0), .IN1(and2_4_out0), .Carry_in(1'b0), .Sum(out_10), .Carry_out(fulladder_1_carry_out));
  FullAdder fulladder_2 (
    .IN0(and2_3_out0), .IN1(and2_5_out0), .Carry_in(fulladder_1_carry_out), .Sum(fulladder_2_sum),
    .Carry_out(fulladder_2_carry_out));
  FullAdder fulladder_3 (
    .IN0(nand_1_out0), .IN1(and2_6_out0), .Carry_in(fulladder_2_carry_out), .Sum(fulladder_3_sum),
    .Carry_out(fulladder_3_carry_out));
  FullAdder fulladder_4 (
    .IN0(1'b1), .IN1(nand_2_out0), .Carry_in(fulladder_3_carry_out), .Sum(fulladder_4_sum),
    .Carry_out(fulladder_4_carry_out));
  AND2 and2_7 (.IN0(in_3), .IN1(in_5), .OUT0(and2_7_out0));
  AND2 and2_8 (.IN0(in_3), .IN1(in_6), .OUT0(and2_8_out0));
  AND2 and2_9 (.IN0(in_3), .IN1(in_7), .OUT0(and2_9_out0));
  NAND nand_3 (.IN0(in_3), .OUT0(nand_3_out0), .IN1(in_8));
  FullAdder fulladder_5 (
    .IN0(fulladder_2_sum), .IN1(and2_7_out0), .Carry_in(1'b0), .Sum(out_11), .Carry_out(fulladder_5_carry_out));
  FullAdder fulladder_6 (
    .IN0(fulladder_3_sum), .IN1(and2_8_out0), .Carry_in(fulladder_5_carry_out), .Sum(fulladder_6_sum),
    .Carry_out(fulladder_6_carry_out));
  FullAdder fulladder_7 (
    .IN0(fulladder_4_sum), .IN1(and2_9_out0), .Carry_in(fulladder_6_carry_out), .Sum(fulladder_7_sum),
    .Carry_out(fulladder_7_carry_out));
  FullAdder fulladder_8 (
    .IN0(fulladder_4_carry_out), .IN1(nand_3_out0), .Carry_in(fulladder_7_carry_out), .Sum(fulladder_8_sum),
    .Carry_out(fulladder_8_carry_out));
  NAND nand_4 (.IN0(in_4), .OUT0(nand_4_out0), .IN1(in_5));
  FullAdder fulladder_9 (
    .IN0(fulladder_6_sum), .IN1(nand_4_out0), .Carry_in(1'b0), .Sum(out_12), .Carry_out(fulladder_9_carry_out));
  NAND nand_5 (.IN0(in_4), .OUT0(nand_5_out0), .IN1(in_6));
  FullAdder fulladder_10 (
    .IN0(fulladder_7_sum), .IN1(nand_5_out0), .Carry_in(fulladder_9_carry_out), .Sum(out_13),
    .Carry_out(fulladder_10_carry_out));
  NAND nand_6 (.IN0(in_4), .OUT0(nand_6_out0), .IN1(in_7));
  FullAdder fulladder_11 (
    .IN0(fulladder_8_sum), .IN1(nand_6_out0), .Carry_in(fulladder_10_carry_out), .Sum(out_14),
    .Carry_out(fulladder_11_carry_out));
  AND2 and2_10 (.IN0(in_4), .IN1(in_8), .OUT0(and2_10_out0));
  FullAdder fulladder_12 (
    .IN0(fulladder_8_carry_out), .IN1(and2_10_out0), .Carry_in(fulladder_11_carry_out), .Sum(out_15),
    .Carry_out(fulladder_12_carry_out));
  HalfAdder halfadder_1 (.IN0(fulladder_12_carry_out), .IN1(1'b1), .Sum(out_16));  // open: Carry_Out
endmodule

module Divider_4bit (
  input  in_1,
  input  in_2,
  input  in_3,
  input  in_4,
  input  in_5,
  input  in_6,
  output out_7,
  output out_8,
  output out_9,
  output out_10
);

  wire and3_1_out0, and3_2_out0, and3_3_out0, and3_4_out0, and3_5_out0, and3_6_out0, and3_7_out0,
       and3_8_out0, and3_9_out0, not_1_out, not_2_out, not_3_out, not_4_out, not_5_out, not_6_out, not_7_out,
       not_8_out, not_9_out, not_10_out, not_11_out, not_12_out, not_13_out, or_1_out0, or_2_out0, or_3_out0;

  not not_1 (not_1_out, in_2);
  not not_2 (not_2_out, in_1);
  not not_3 (not_3_out, in_2);
  not not_4 (not_4_out, in_1);
  not not_5 (not_5_out, in_2);
  not not_6 (not_6_out, in_1);
  not not_7 (not_7_out, in_2);
  not not_8 (not_8_out, in_1);
  not not_9 (not_9_out, in_2);
  not not_10 (not_10_out, in_1);
  not not_11 (not_11_out, in_2);
  not not_12 (not_12_out, in_2);
  not not_13 (not_13_out, in_1);
  AND3 and3_1 (.IN0(in_3), .IN1(not_1_out), .OUT0(and3_1_out0), .IN2(not_2_out));
  AND3 and3_2 (.IN0(in_4), .IN1(not_3_out), .OUT0(and3_2_out0), .IN2(in_1));
  AND3 and3_3 (.IN0(in_5), .IN1(in_2), .OUT0(and3_3_out0), .IN2(not_4_out));
  AND3 and3_4 (.IN0(in_6), .IN1(in_2), .OUT0(and3_4_out0), .IN2(in_1));
  AND3 and3_5 (.IN0(in_4), .IN1(not_5_out), .OUT0(and3_5_out0), .IN2(not_6_out));
  AND3 and3_6 (.IN0(in_5), .IN1(not_7_out), .OUT0(and3_6_out0), .IN2(in_1));
  AND3 and3_7 (.IN0(in_6), .IN1(in_2), .OUT0(and3_7_out0), .IN2(not_8_out));
  AND3 and3_8 (.IN0(in_5), .IN1(not_9_out), .OUT0(and3_8_out0), .IN2(not_10_out));
  AND3 and3_9 (.IN0(in_6), .IN1(not_11_out), .OUT0(and3_9_out0), .IN2(in_1));
  AND3 and3_10 (.IN0(in_6), .IN1(not_12_out), .OUT0(out_10), .IN2(not_13_out));
  OR or_1 (.IN0(and3_1_out0), .IN1(and3_2_out0), .OUT0(or_1_out0));
  OR or_2 (.IN0(and3_3_out0), .IN1(and3_4_out0), .OUT0(or_2_out0));
  OR or_3 (.IN0(and3_5_out0), .IN1(and3_6_out0), .OUT0(or_3_out0));
  OR or_4 (.IN0(and3_8_out0), .IN1(and3_9_out0), .OUT0(out_9));
  OR or_5 (.IN0(or_1_out0), .IN1(or_2_out0), .OUT0(out_7));
  OR or_6 (.IN0(or_3_out0), .IN1(and3_7_out0), .OUT0(out_8));
endmodule
