// Logisim project Standard_Cells.circ as structural Verilog: 8 circuits, main circuit NAND
module NAND (
  input  IN0,
  input  IN1,
  output OUT0
);

  wire transistor_4_out;

  Transistor transistor_1 (.in(1'b1), .out(OUT0), .gate(IN1));
  Transistor #(.\type ("n")) transistor_2 (.in(transistor_4_out), .out(OUT0), .gate(IN1));
  Transistor transistor_3 (.in(1'b1), .out(OUT0), .gate(IN0));
  Transistor #(.\type ("n")) transistor_4 (.in(1'b0), .out(transistor_4_out), .gate(IN0));
endmodule

module XOR2 (
  input  IN0,
  input  IN1,
  output OUT0
);

  wire transistor_1_out, transistor_5_out;

  Transistor #(.\type ("n")) transistor_1 (.in(1'b1), .out(transistor_1_out), .gate(IN0));
  Transistor transistor_2 (.in(1'b0), .out(transistor_1_out), .gate(IN0));
  Transistor #(.gate("br")) transistor_3 (.in(transistor_1_out), .out(OUT0), .gate(IN1));
  Transistor #(.\type ("n")) transistor_4 (.in(transistor_5_out), .out(OUT0), .gate(IN1));
  Transistor transistor_5 (.in(1'b1), .out(transistor_5_out), .gate(transistor_1_out));
  Transistor #(.\type ("n")) transistor_6 (.in(1'b0), .out(transistor_5_out), .gate(transistor_1_out));
endmodule

module XOR3 (
  input  IN0,
  input  IN1,
  input  IN2,
  output OUT0
);

  wire transistor_1_out, transistor_3_out, transistor_5_out, transistor_7_out, transistor_10_out;

  Transistor #(.\type ("n")) transistor_1 (.in(1'b1), .out(transistor_1_out), .gate(IN0));
  Transistor transistor_2 (.in(1'b0), .out(transistor_1_out), .gate(IN0));
  Transistor #(.gate("br")) transistor_3 (.in(transistor_1_out), .out(transistor_3_out), .gate(IN2));
  Transistor #(.\type ("n")) transistor_4 (.in(transistor_5_out), .out(transistor_3_out), .gate(IN2));
  Transistor transistor_5 (.in(1'b1), .out(transistor_5_out), .gate(transistor_1_out));
  Transistor #(.\type ("n")) transistor_6 (.in(1'b0), .out(transistor_5_out), .gate(transistor_1_out));
  Transistor #(.\type ("n")) transistor_7 (.in(1'b1), .out(transistor_7_out), .gate(transistor_3_out));
  Transistor transistor_8 (.in(1'b0), .out(transistor_7_out), .gate(transistor_3_out));
  Transistor #(.gate("br")) transistor_9 (.in(transistor_7_out), .out(OUT0), .gate(IN1));
  Transistor transistor_10 (.in(1'b1), .out(transistor_10_out), .gate(transistor_7_out));
  Transistor #(.\type ("n")) transistor_11 (.in(1'b0), .out(transistor_10_out), .gate(transistor_7_out));
  Transistor #(.\type ("n")) transistor_12 (.in(transistor_10_out), .out(OUT0), .gate(IN1));
endmodule

module AND2 (
  input  IN0,
  input  IN1,
  output OUT0
);

  wire transistor_1_out, transistor_4_out;

  Transistor transistor_1 (.in(1'b1), .out(transistor_1_out), .gate(IN1));
  Transistor #(.\type ("n")) transistor_2 (.in(transistor_4_out), .out(transistor_1_out), .gate(IN1));
  Transistor transistor_3 (.in(1'b1), .out(transistor_1_out), .gate(IN0));
  Transistor #(.\type ("n")) transistor_4 (.in(1'b0), .out(transistor_4_out), .gate(IN0));
  Transistor transistor_5 (.in(1'b1), .out(OUT0), .gate(transistor_1_out));
  Transistor #(.\type ("n")) transistor_6 (.in(1'b0), .out(OUT0), .gate(transistor_1_out));
endmodule

module AND3 (
  input  IN0,
  input  IN1,
  input  IN2,
  output OUT0
);

  wire transistor_1_out, transistor_3_out, transistor_6_out;

  Transistor #(.\type ("n")) transistor_1 (.in(transistor_3_out), .out(transistor_1_out), .gate(IN2));
  Transistor transistor_2 (.in(1'b1), .out(transistor_1_out), .gate(IN2));
  Transistor #(.\type ("n")) transistor_3 (.in(transistor_6_out), .out(transistor_3_out), .gate(IN1));
  Transistor transistor_4 (.in(1'b1), .out(transistor_1_out), .gate(IN0));
  Transistor transistor_5 (.in(1'b1), .out(transistor_1_out), .gate(IN1));
  Transistor #(.\type ("n")) transistor_6 (.in(1'b0), .out(transistor_6_out), .gate(IN0));
  Transistor transistor_7 (.in(1'b1), .out(OUT0), .gate(transistor_1_out));
  Transistor #(.\type ("n")) transistor_8 (.in(1'b0), .out(OUT0), .gate(transistor_1_out));
endmodule

module OR (
  input  IN0,
  input  IN1,
  output OUT0
);

  wire transistor_1_out, transistor_2_out;

  Transistor #(.\type ("n")) transistor_1 (.in(1'b0), .out(transistor_1_out), .gate(IN0));
  Transistor transistor_2 (.in(1'b1), .out(transistor_2_out), .gate(IN0));
  Transistor transistor_3 (.in(transistor_2_out), .out(transistor_1_out), .gate(IN1));
  Transistor #(.\type ("n")) transistor_4 (.in(1'b0), .out(transistor_1_out), .gate(IN1));
  Transistor transistor_5 (.in(1'b1), .out(OUT0), .gate(transistor_1_out));
  Transistor #(.\type ("n")) transistor_6 (.in(1'b0), .out(OUT0), .gate(transistor_1_out));
endmodule

module HalfAdder (
  input  IN0,
  input  IN1,
  output Sum,
  output Carry_Out
);

  wire transistor_1_out, transistor_5_out, transistor_10_out;

  Transistor #(.\type ("n")) transistor_1 (.in(1'b1), .out(transistor_1_out), .gate(IN0));
  Transistor transistor_2 (.in(1'b0), .out(transistor_1_out), .gate(IN0));
  Transistor #(.gate("br")) transistor_3 (.in(transistor_1_out), .out(Sum), .gate(IN1));
  Transistor #(.\type ("n")) transistor_4 (.in(transistor_10_out), .out(Carry_Out), .gate(IN1));
  Transistor transistor_5 (.in(1'b1), .out(transistor_5_out), .gate(transistor_1_out));
  Transistor #(.\type ("n")) transistor_6 (.in(1'b0), .out(transistor_5_out), .gate(transistor_1_out));
  Transistor #(.\type ("n")) transistor_7 (.in(transistor_5_out), .out(Sum), .gate(IN1));
  Transistor transistor_8 (.in(1'b0), .out(Carry_Out), .gate(IN1));
  Transistor transistor_9 (.in(1'b0), .out(Carry_Out), .gate(IN0));
  Transistor #(.\type ("n")) transistor_10 (.in(1'b1), .out(transistor_10_out), .gate(IN0));
endmodule

module FullAdder (
  input  IN0,
  input  Carry_in,
  input  IN1,
  output Sum,
  output Carry_out
);

  wire transistor_1_out, transistor_3_out, transistor_4_out, transistor_5_out, transistor_10_out,
       transistor_11_out, transistor_14_out, transistor_19_out, transistor_20_out, transistor_23_out;

  Transistor #(.\type ("n")) transistor_1 (.in(1'b1), .out(transistor_1_out), .gate(IN0));
  Transistor transistor_2 (.in(1'b0), .out(transistor_1_out), .gate(IN0));
  Transistor #(.gate("br")) transistor_3 (.in(transistor_1_out), .out(transistor_3_out), .gate(IN1));
  Transistor #(.\type ("n")) transistor_4 (.in(transistor_10_out), .out(transistor_4_out), .gate(IN1));
  Transistor transistor_5 (.in(1'b1), .out(transistor_5_out), .gate(transistor_1_out));
  Transistor #(.\type ("n")) transistor_6 (.in(1'b0), .out(transistor_5_out), .gate(transistor_1_out));
  Transistor #(.\type ("n")) transistor_7 (.in(transistor_5_out), .out(transistor_3_out), .gate(IN1));
  Transistor transistor_8 (.in(1'b0), .out(transistor_4_out), .gate(IN0));
  Transistor transistor_9 (.in(1'b0), .out(transistor_4_out), .gate(IN1));
  Transistor #(.\type ("n")) transistor_10 (.in(1'b1), .out(transistor_10_out), .gate(IN0));
  Transistor #(.\type ("n")) transistor_11 (.in(1'b1), .out(transistor_11_out), .gate(transistor_3_out));
  Transistor transistor_12 (.in(1'b0), .out(transistor_11_out), .gate(transistor_3_out));
  Transistor #(.gate("br")) transistor_13 (.in(transistor_11_out), .out(Sum), .gate(Carry_in));
  Transistor #(.gate("br")) transistor_14 (.in(1'b0), .out(transistor_14_out), .gate(transistor_4_out));
  Transistor #(.\type ("n")) transistor_15 (.in(1'b1), .out(Carry_out), .gate(transistor_4_out));
  Transistor #(.\type ("n")) transistor_16 (.in(transistor_20_out), .out(Sum), .gate(Carry_in));
  Transistor #(.gate("br")) transistor_17 (.in(transistor_14_out), .out(Carry_out), .gate(transistor_19_out));
  Transistor #(.\type ("n")) transistor_18 (.in(1'b1), .out(Carry_out), .gate(transistor_19_out));
  Transistor #(.\type ("n")) transistor_19 (.in(transistor_23_out), .out(transistor_19_out), .gate(Carry_in));
  Transistor transistor_20 (.in(1'b1), .out(transistor_20_out), .gate(transistor_11_out));
  Transistor #(.\type ("n")) transistor_21 (.in(1'b0), .out(transistor_20_out), .gate(transistor_11_out));
  Transistor transistor_22 (.in(1'b0), .out(transistor_19_out), .gate(Carry_in));
  Transistor #(.\type ("n")) transistor_23 (.in(1'b1), .out(transistor_23_out), .gate(transistor_3_out));
  Transistor transistor_24 (.in(1'b0), .out(transistor_19_out), .gate(transistor_3_out));
endmodule
